# Fritzing sketch circuit with AC motor (saved by Fritzing 0.9.5d)
breadboards: 1

parts:
  TP1 = TP4056 [chip_label=TP4056 package="DIP (Dual Inline) [THT]"]
  TP2 = TP4056 [chip_label=TP4056 package="DIP (Dual Inline) [THT]"]
  pannello_solare = SOLAR-IXYS [package=solarbit-12x1]
  Buck-boost = SDB628
  diodo = Schottky Diode [part_number=1N5817 package="Melf DO-213 AB [SMD]"]
  Batteria1 = battery_holder_single_18650
  Batteria2 = battery_holder_single_18650
  Batteria3 = battery_holder_single_18650
  diodi_a_ponte = bridge rectifier round [package="round [THT]"]
  Motore_12V/pendolo = DC Motor
  Condensatore = Capacitor Polarized [package=cpol-radial-1000uf-25v]

nets:
  N1: TP1.pin1, diodo.cathode
  N2: TP1.pin2, pannello_solare.A
  N3: TP1.pin4, TP2.pin4, Batteria1.+#1, Batteria2.+#1, Batteria3.+#1
  N4: TP1.pin5, TP2.pin5, Batteria1.+#0, Batteria2.+#0, Batteria3.+#0
  N5: TP2.pin1, Buck-boost.Pin_5
  N6: TP2.pin2, Buck-boost.Pin_4
  N7: pannello_solare.C, diodo.anode
  N8: Buck-boost.Pin_1, diodi_a_ponte.DC+, Condensatore.+
  N9: Buck-boost.Pin_3, diodi_a_ponte.DC-, Condensatore.-
  N10: diodi_a_ponte.AC#0, Motore_12V/pendolo.pin_2
  N11: diodi_a_ponte.AC#1, Motore_12V/pendolo.pin_1

custom parts:
  TP4056: A DIP stand-in part for whatever IC you want. With 6 pins on a 300mil dual inline package (DIP) footprint.
  SDB628: Boost buck regulator module.
  battery_holder_single_18650: single 18650 battery holder
